# Fritzing sketch Schematics (saved by Fritzing 0.9.3b)
perfboards: 1

parts:
  U1 = NodeMCU V1.0
  LED1 = LED - 5mm [color="Red (633nm)" package="5 mm [THT]"]
  LED2 = LED - 5mm [color="Red (633nm)" package="5 mm [THT]"]
  J1 = female pin header, 3 pins [form="♀ (female)"]
  R1 = Resistor [tolerance=±5% resistance=150 package=THT]
  J2 = female pin header, 2 pins [form="♀ (female)"]
  J3 = female pin header, 2 pins [form="♀ (female)"]
  R2 = Resistor [tolerance=±5% resistance=150 package=THT]
  VCC1 = Battery block 9V
  S7 = Toggle Switch [package=THT]

nets:
  N1: U1.GND, LED1.cathode, LED2.cathode, J1.pin1, J2.pin1, J3.pin1, VCC1.-
  N2: U1.D5, J1.pin2, R1.Pin_1
  N3: U1.D7, J1.pin3, R2.Pin_1
  N4: U1.Vin, S7.L2
  N5: LED1.anode, J2.pin2, R2.Pin_0
  N6: LED2.anode, R1.Pin_0, J3.pin2
  N7: VCC1.+, S7.COM

custom parts:
  NodeMCU V1.0: ESP8266 based NodeMCU
